# Fritzing sketch layout-rpi2-3 (saved by Fritzing 0.9.3b)
breadboards: 1

parts:
  R1 = Rotary Potentiometer (Small) [maximum_resistance=100kΩ package=THT]
  S1 = Pushbutton [package="[THT]"]
  LCD1 = LCD screen
  Raspberry_Pi_2 = Raspberry Pi 3 [part_number=RPI-3-V1.2]

nets:
  VSS: R1.leg1, S1.Pin_1, S1.Pin_2, LCD1.VSS, LCD1.R/W, Raspberry_Pi_2.GND
  N1: R1.wiper, LCD1.V0
  VDD: R1.leg2, LCD1.VDD, LCD1.LED+, Raspberry_Pi_2.5V
  N2: S1.Pin_3, S1.Pin_4, Raspberry_Pi_2.GIPO11
  N3: LCD1.RS, Raspberry_Pi_2.GIPO22
  N4: LCD1.E, Raspberry_Pi_2.GIPO17
  N5: LCD1.DB4, Raspberry_Pi_2.GIPO25
  N6: LCD1.DB5, Raspberry_Pi_2.GIPO24
  N7: LCD1.DB6, Raspberry_Pi_2.GIPO23
  N8: LCD1.DB7, Raspberry_Pi_2.GIPO18
  N9: LCD1.LED-, Raspberry_Pi_2.GIPO4
