# Fritzing sketch layout (saved by Fritzing 0.9.3b)
breadboards: 1

parts:
  R1 = Rotary Potentiometer (Small) [maximum_resistance=100kΩ package=THT]
  S1 = Pushbutton [package="[THT]"]
  Raspberry_Pi_B_rev1 = Raspberry Pi B rev2
  LCD1 = LCD screen

nets:
  GND: R1.leg1, S1.Pin_1, S1.Pin_2, Raspberry_Pi_B_rev1.GND, Raspberry_Pi_B_rev1.GPIO_17, LCD1.VSS, LCD1.R/W, LCD1.E
  N1: R1.wiper, LCD1.V0
  5V: R1.leg2, Raspberry_Pi_B_rev1.5V, LCD1.VDD, LCD1.LED+
  N2: S1.Pin_3, S1.Pin_4, Raspberry_Pi_B_rev1.GPIO_11, Raspberry_Pi_B_rev1.GPIO_8
  N3: Raspberry_Pi_B_rev1.GPIO_23, LCD1.DB6
  N4: Raspberry_Pi_B_rev1.GPIO_14, Raspberry_Pi_B_rev1.GPIO_4, LCD1.LED-
  N5: Raspberry_Pi_B_rev1.GPIO_18, LCD1.DB7
  N6: Raspberry_Pi_B_rev1.GPIO_22, LCD1.RS
  N7: Raspberry_Pi_B_rev1.GPIO_24, LCD1.DB5
  N8: Raspberry_Pi_B_rev1.GPIO_25, LCD1.DB4
